// Logisim project file.circ as structural Verilog: 3 circuits, main circuit main
module main (
);

  wire registerfile_1_p4;
  wire [3:0] alu_control_1_out_3;
  wire [4:0] multiplexer_1_out;
  wire [5:0] instr__0_5;
  wire [31:0] bit_extender_1_out, mips_alu_1_p4, mips_alu_2_p4, multiplexer_2_out, multiplexer_3_out,
       register_1_q, registerfile_1_p5, shifter_1_out;
  wire [31:6] undriven;

  Register #(.width(32)) register_1 (.D(multiplexer_3_out), .en(1'b1), .Q(register_1_q));  // open: clk, clr
  RAM #(.dataWidth(32)) ram_1 ();  // open: addr, data, sel, clk, ld, clr
  // MIPS_ALU mips_alu_1: pin names not known; wires that end beside it: register_1_q, 32'h4, 4'b0010, mips_alu_1_p4
  Multiplexer #(.width(5), .enable("false")) multiplexer_1 (
    .in0(undriven[15:11]), .in1(undriven[20:16]), .out(multiplexer_1_out));  // open: sel
  Control control_1 (.in_1(undriven[31:26]));  // open: RegDst, Branch, MemRead, MemtoReg, ALUOP, MemWrite, ALUSrc, RegWrite
  assign bit_extender_1_out = {{16{undriven[15]}}, {undriven[15:6], instr__0_5}};  // Bit_Extender bit_extender_1
  // RegisterFile registerfile_1: pin names not known; wires that end beside it: multiplexer_1_out, undriven[25:21], undriven[20:16], registerfile_1_p4, registerfile_1_p5
  Shifter #(.width(32)) shifter_1 (.in(bit_extender_1_out), .\dist (5'b00010), .out(shifter_1_out));
  Multiplexer #(.width(32), .enable("false")) multiplexer_2 (
    .in0(bit_extender_1_out), .in1(registerfile_1_p5), .out(multiplexer_2_out));  // open: sel
  ALU_control alu_control_1 (.From_Instruction(instr__0_5), .out_3(alu_control_1_out_3));  // open: in_1
  // MIPS_ALU mips_alu_2: pin names not known; wires that end beside it: mips_alu_1_p4, shifter_1_out, 4'b0010, mips_alu_2_p4
  // MIPS_ALU mips_alu_3: pin names not known; wires that end beside it: registerfile_1_p4, multiplexer_2_out, alu_control_1_out_3
  Multiplexer #(.width(32), .enable("false")) multiplexer_3 (
    .in0(mips_alu_1_p4), .in1(mips_alu_2_p4), .out(multiplexer_3_out));  // open: sel

  // Notes on the sheet:
  //   PC
  //   32 bit instruction should come here
  //   Control
  //   Alu Control
endmodule

module Control (
  input  [5:0] in_1,
  output RegDst,
  output Branch,
  output MemRead,
  output MemtoReg,
  output ALUOP,
  output MemWrite,
  output ALUSrc,
  output RegWrite
);
endmodule

module ALU_control (
  input  in_1,
  input  [5:0] From_Instruction,
  output [3:0] out_3
);
endmodule
